# Fritzing sketch PIRsense-buzzr (saved by Fritzing 0.9.3b)
breadboards: 1

parts:
  PIR1 = PIR sensor
  R1 = Resistor [tolerance=±5% resistance=220 package="0805 [SMD]"]
  Part1 = Arduino Uno (Rev3) - ICSP
  LED3 = LED - 5mm [color="Red (633nm)" package="5 mm [THT]"]
  J1 = Piezo Speaker

nets:
  VDD: PIR1.VDD, Part1.5V
  N1: PIR1.SIG, Part1.D2
  GND: PIR1.GND, Part1.GND, LED3.anode, J1.pin1
  N2: R1.Pin_0, Part1.D5_PWM
  N3: R1.Pin_1, LED3.cathode, J1.pin2
